# Fritzing sketch autoPlanter (saved by Fritzing 1.0.0rc)
breadboards: 3

parts:
  Breadboard4 = Breadboard Split Power
  Breadboard5 = Breadboard Split Power
  A1 = Particle - Photon2
  Neopixel1 = Adafruit RBG Smart Neopixel [package="DIP (Dual Inline) [THT]"]
  Neopixel2 = Adafruit RBG Smart Neopixel [package="DIP (Dual Inline) [THT]"]
  Neopixel3 = Adafruit RBG Smart Neopixel [package="DIP (Dual Inline) [THT]"]
  Neopixel4 = Adafruit RBG Smart Neopixel [package="DIP (Dual Inline) [THT]"]
  Part1 = 12 NeoPixel Ring [part_number=1643]
  M1 = BMP280
  OLED_I2C1 = OLED 128x64 I2C Monochrome Display
  Q1 = PNP-Transistor [package="TO92 [THT]"]
  R1 = Resistor [tolerance=±5% power=0.25W resistance=1.8k package=THT]
  R2 = Resistor [tolerance=±5% power=0.25W resistance=3.3k package=THT]
  SENS1 = SoilWatch 10
  Part2 = MQ-131 breakout
  Grove1 = Grove Dust Sensor
  S1 = Pushbutton [package="[THT]"]
  M2 = DC Motor [voltage_(max)=6V voltage_(min)=3V]
  A2 = 1 chan 3v relay module
  Q2 = PNP-Transistor [package="TO92 [THT]"]
  R3 = Resistor [tolerance=±5% power=0.25W resistance=1.8k package=THT]
  R4 = Resistor [tolerance=±5% power=0.25W resistance=3.3k package=THT]

nets:
  VCC: Breadboard4.pin15Y, Breadboard4.pin17Y, Breadboard4.pin21Y, Breadboard4.pin29Y, Breadboard5.pin3Y, Breadboard5.pin15Y, Breadboard5.pin17Y, Breadboard5.pin22Y, Breadboard5.pin24Y, Breadboard5.pin29Y, A1.Pin_2, A1.Pin_31, M1.VIN, OLED_I2C1.VDD, SENS1.VCC, Part2.VCC, A2.pin_1
  GND: Breadboard4.pin20Z, Breadboard4.pin29Z, Breadboard5.pin3Z, Breadboard5.pin15Z, Breadboard5.pin17Z, Breadboard5.pin22Z, Breadboard5.pin24Z, Breadboard5.pin28Z, A1.Pin_4, A1.Pin_35, M1.GND, OLED_I2C1.GND, Q1.C, SENS1.OUT, Part2.GND, M2.pin_1, A2.pin_3, Q2.C, R4.Pin_1
  N1: A1.Pin_7, SENS1.GND
  N2: A1.Pin_8, Part2.AO
  N3: A1.Pin_9, Q2.B, R4.Pin_0
  N4: A1.Pin_17, M1.SDA, OLED_I2C1.SDA
  N5: A1.Pin_18, M1.SCL, OLED_I2C1.SCK
  N6: A1.Pin_19, R2.Pin_0
  GND_2: A1.Pin_22, Neopixel1.G, Neopixel2.G, Neopixel3.G, Neopixel4.G, Part1.GND, Grove1.GND, S1.Pin_3, S1.Pin_4
  N7: A1.Pin_23, A1.Pin_37, Grove1.SIG
  VDD: A1.Pin_26, Neopixel1.+, Neopixel2.+, Neopixel3.+, Neopixel4.+, Part1.VDD, R1.Pin_0, Grove1.VCC, S1.Pin_1, S1.Pin_2, A2.pin_7, R3.Pin_1
  N8: Neopixel1.In, Q1.E, R1.Pin_1
  N9: Neopixel1.O, Neopixel2.In
  N10: Neopixel2.O, Neopixel3.In
  N11: Neopixel3.O, Neopixel4.In
  N12: Neopixel4.O, Part1.IN
  N13: Q1.B, R2.Pin_1
  N14: M2.pin_2, A2.pin_6
  N15: A2.pin_2, Q2.E, R3.Pin_0

custom parts:
  Breadboard Split Power: A custom 6 pin per group power supply strip where the top row (ground) is all bussed together and the bottom row (+V) is split in two groups of 12 pins. This version is modified to be a loadable part and was rescaled to be on the standard 1px = 1thou grid with the size set in inches
  Particle - Photon2: The Photon 2 is a microcontroller and Wi-Fi networking developed by particle. Features: 802.11a/b/g/n Wi-Fi, 2.4 GHz and 5 GHz Integrated PCB antenna Integrated U.FL connector for external antenna Integrated RF switch BLE 5 using same antenna as Wi-Fi Realtek RTL8721DM MCU ARM Cortex M33 CPU, 200 MHz 2048 KB (2 MB) user application maximum size 3072 KB (3 MB) of RAM available to user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
  12 NeoPixel Ring: 12 ultra bright smart LED NeoPixels are arranged in a circle with 1.5" (37mm) outer diameter. The rings are 'chainable' - connect the output pin of one to the input pin of another. Use only one microcontroller pin to control as many as you can chain together! Each LED is addressable as the driver chip is inside the LED. Each one has ~18mA constant current drive so the color will be very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
  BMP280: Temperature Humidity Barometric presure Sensor, I2C
  SoilWatch 10: SoilWatch 10 - Capacitive soil moisture sensor
  MQ-131 breakout: SKU: 101282
  Grove Dust Sensor: PPD42 Grove Dust Sensor
  Pushbutton: A generic pushbutton.
  1 chan 3v relay module: Single 3V relay isolated drive control module High level drive board.
